// Logisim project GHR.circ as structural Verilog: 1 circuit, main circuit main
module main (
  input  entrada,
  output [7:0] out_2
);

  wire clock_1_out;

  Clock clock_1 (.out(clock_1_out));
  D_Flip_Flop GHR_7 (.clk(clock_1_out), .D(entrada), .Q(out_2[7]));  // open: Qn, preset, en, reset
  D_Flip_Flop GHR_6 (.clk(clock_1_out), .D(out_2[7]), .Q(out_2[6]));  // open: Qn, preset, en, reset
  D_Flip_Flop GHR_5 (.clk(clock_1_out), .D(out_2[6]), .Q(out_2[5]));  // open: Qn, preset, en, reset
  D_Flip_Flop GHR_4 (.clk(clock_1_out), .D(out_2[5]), .Q(out_2[4]));  // open: Qn, preset, en, reset
  D_Flip_Flop GHR_3 (.clk(clock_1_out), .D(out_2[4]), .Q(out_2[3]));  // open: Qn, preset, en, reset
  D_Flip_Flop GHR_2 (.clk(clock_1_out), .D(out_2[3]), .Q(out_2[2]));  // open: Qn, preset, en, reset
  D_Flip_Flop GHR_1 (.clk(clock_1_out), .D(out_2[2]), .Q(out_2[1]));  // open: Qn, preset, en, reset
  D_Flip_Flop GHR_0 (.clk(clock_1_out), .D(out_2[1]), .Q(out_2[0]));  // open: Qn, preset, en, reset
endmodule
