// Logisim project Perceptron.circ as structural Verilog: 3 circuits, main circuit main
module main (
  input  hit_miss
);

  wire adder_1_out, clock_1_out, multiplexer_1_out, multiplexer_2_out, negator_1_out, negator_2_out;
  wire [7:0] GHR_out_3;
  wire [9:0] ram_1_data;
  wire [15:0] PC_out_3;

  Clock clock_1 (.out(clock_1_out));
  PC PC (.in_1(clock_1_out), .out_3(PC_out_3));  // open: in_2
  GHR GHR (.clk(clock_1_out), .entrada(hit_miss), .out_3(GHR_out_3));
  RAM #(.addrWidth(10), .dataWidth(10)) ram_1 (.addr(PC_out_3[11:2]), .data(ram_1_data));  // open: sel, clk, ld, clr
  Multiplexer multiplexer_1 (
    .in0(ram_1_data[1]), .in1(negator_1_out), .out(multiplexer_1_out), .sel(GHR_out_3[0]));  // open: en
  Negator #(.width(1)) negator_1 (.in(ram_1_data[1]), .out(negator_1_out));
  Negator #(.width(1)) negator_2 (.in(ram_1_data[2]), .out(negator_2_out));
  Multiplexer multiplexer_2 (
    .in0(ram_1_data[2]), .in1(negator_2_out), .out(multiplexer_2_out), .sel(GHR_out_3[1]));  // open: en
  Adder #(.width(1)) adder_1 (
    .a(multiplexer_1_out), .b(multiplexer_2_out), .out(adder_1_out), .cin(ram_1_data[0]));  // open: cout
  Register #(.width(1)) Score__u (.D(adder_1_out));  // open: en, Q, clk, clr

  // Notes on the sheet:
  //   32 bits
  //   /
  //   11:2
  //   10  bits
  //   /
  //   Tabela de Pesos
  //   BIAS
  //   8 bits
  //   /
  //   -1
  //   8 bits
  //   /
  //   W(1)
  //   -1
  //   W(2)
  //   somador Σ
endmodule

module GHR (
  input  clk,
  input  entrada,
  output [7:0] out_3
);

  D_Flip_Flop GHR_7 (.clk(clk), .D(entrada), .Q(out_3[7]));  // open: Qn, preset, en, reset
  D_Flip_Flop GHR_6 (.clk(clk), .D(out_3[7]), .Q(out_3[6]));  // open: Qn, preset, en, reset
  D_Flip_Flop GHR_5 (.clk(clk), .D(out_3[6]), .Q(out_3[5]));  // open: Qn, preset, en, reset
  D_Flip_Flop GHR_4 (.clk(clk), .D(out_3[5]), .Q(out_3[4]));  // open: Qn, preset, en, reset
  D_Flip_Flop GHR_3 (.clk(clk), .D(out_3[4]), .Q(out_3[3]));  // open: Qn, preset, en, reset
  D_Flip_Flop GHR_1 (.clk(clk), .D(out_3[2]), .Q(out_3[1]));  // open: Qn, preset, en, reset
  D_Flip_Flop GHR_2 (.clk(clk), .D(out_3[3]), .Q(out_3[2]));  // open: Qn, preset, en, reset
  D_Flip_Flop GHR_0 (.clk(clk), .D(out_3[1]), .Q(out_3[0]));  // open: Qn, preset, en, reset
endmodule

module PC (
  input  in_1,
  input  in_2,
  output [15:0] out_3
);

  Counter #(.width(16), .max('hffff)) counter_1 (.Q(out_3), .clk(in_1), .clr(in_2));  // open: load, D, count, carry
endmodule
