// Logisim project PerceptronWithTrainPredictionAndNear-train(xnor).circ as structural Verilog: 3 circuits, main circuit main
module main (
  input  hit_miss
);

  wire adder_2_out, clock_1_out, comparator_1_eq, comparator_1_lt, multiplexer_1_out, multiplexer_2_out,
       multiplexer_3_out, multiplexer_4_out, negator_1_out, negator_2_out, not_1_out, or_1_out, or_2_out,
       xnor_1_out, xnor_2_out;
  wire [7:0] GHR_out_3;
  wire [8:0] multiplexer_5_out, negator_3_out, Score__u_q;
  wire [9:0] ram_1_data;
  wire [15:0] PC_out_3;

  Clock clock_1 (.out(clock_1_out));
  PC PC (.in_1(clock_1_out), .out_3(PC_out_3));  // open: in_2
  GHR GHR (.clk(clock_1_out), .entrada(hit_miss), .out_3(GHR_out_3));
  not not_1 (not_1_out, 1'b1);
  RAM #(.addrWidth(10), .dataWidth(10)) ram_1 (.addr(PC_out_3[11:2]), .data(ram_1_data));  // open: sel, clk, ld, clr
  Multiplexer multiplexer_1 (
    .in0(GHR_out_3[0]), .in1(not_1_out), .out(multiplexer_1_out), .sel(multiplexer_2_out), .en(or_1_out));
  Multiplexer multiplexer_2 (
    .in0(GHR_out_3[0]), .in1(GHR_out_3[0]), .out(multiplexer_2_out), .en(or_1_out));  // open: sel
  Adder #(.width(1)) adder_1 (.a(ram_1_data[1]), .b(xnor_1_out));  // open: out, cin, cout
  xnor xnor_1 (xnor_1_out, multiplexer_1_out, multiplexer_2_out);
  Multiplexer #(.enable("false")) multiplexer_3 (
    .in0(ram_1_data[1]), .in1(negator_1_out), .out(multiplexer_3_out), .sel(GHR_out_3[0]));
  Negator #(.width(1)) negator_1 (.in(ram_1_data[1]), .out(negator_1_out));
  Negator #(.width(1)) negator_2 (.in(ram_1_data[2]), .out(negator_2_out));
  Multiplexer #(.enable("false")) multiplexer_4 (
    .in0(ram_1_data[2]), .in1(negator_2_out), .out(multiplexer_4_out), .sel(GHR_out_3[1]));
  Adder #(.width(1)) adder_2 (
    .a(multiplexer_3_out), .b(multiplexer_4_out), .out(adder_2_out), .cin(ram_1_data[0]));  // open: cout
  Negator #(.width(1)) negator_3 (.in(Score__u_q[0]), .out(negator_3_out[0]));
  Register #(.width(1)) Score__u (.D(adder_2_out), .Q(Score__u_q[0]));  // open: en, clk, clr
  Multiplexer #(.width(9), .enable("false")) multiplexer_5 (
    .in0(Score__u_q), .in1(negator_3_out), .out(multiplexer_5_out), .sel(Score__u_q[1]));
  Comparator #(.width(9)) comparator_1 (
    .a(multiplexer_5_out), .b(9'h1d), .eq(comparator_1_eq), .lt(comparator_1_lt));  // open: gt
  xnor xnor_2 (xnor_2_out, Score__u_q[1], hit_miss);
  or or_1 (or_1_out, xnor_2_out, or_2_out);
  or or_2 (or_2_out, comparator_1_eq, comparator_1_lt);
  // Pins of 1 and 2 and 9 bits meet at Score__u_q
  // Pins of 9 and 10 bits meet at ram_1_data
  // Pins of 1 and 9 bits meet at negator_3_out

  // Notes on the sheet:
  //   32 bits
  //   /
  //   11:2
  //   10  bits
  //   /
  //   x_i
  //   Tabela de Pesos
  //   W_i(novo) = W_i(atual) + (d*x_i)
  //   d
  //   train enable
  //   BIAS
  //   8 bits
  //   /
  //   -1
  //   8 bits
  //   /
  //   w_i
  //   W(1)
  //   -1
  //   W(2)
  //   score module (|u|)
  //   somador Σ
  //   hit/miss
  //   -1
  //   Threshold (29 em hexa)
  //   y
  //   train enable
endmodule

module GHR (
  input  clk,
  input  entrada,
  output [7:0] out_3
);

  D_Flip_Flop GHR_7 (.clk(clk), .D(entrada), .Q(out_3[7]));  // open: Qn, preset, en, reset
  D_Flip_Flop GHR_6 (.clk(clk), .D(out_3[7]), .Q(out_3[6]));  // open: Qn, preset, en, reset
  D_Flip_Flop GHR_5 (.clk(clk), .D(out_3[6]), .Q(out_3[5]));  // open: Qn, preset, en, reset
  D_Flip_Flop GHR_4 (.clk(clk), .D(out_3[5]), .Q(out_3[4]));  // open: Qn, preset, en, reset
  D_Flip_Flop GHR_3 (.clk(clk), .D(out_3[4]), .Q(out_3[3]));  // open: Qn, preset, en, reset
  D_Flip_Flop GHR_2 (.clk(clk), .D(out_3[3]), .Q(out_3[2]));  // open: Qn, preset, en, reset
  D_Flip_Flop GHR_1 (.clk(clk), .D(out_3[2]), .Q(out_3[1]));  // open: Qn, preset, en, reset
  D_Flip_Flop GHR_0 (.clk(clk), .D(out_3[1]), .Q(out_3[0]));  // open: Qn, preset, en, reset
endmodule

module PC (
  input  in_1,
  input  in_2,
  output [15:0] out_3
);

  Counter #(.width(16), .max('hffff)) counter_1 (.Q(out_3), .clk(in_1), .clr(in_2));  // open: load, D, count, carry
endmodule
