// Logisim project PerceptronWorking.circ as structural Verilog: 3 circuits, main circuit main
module main (
  input  in_1,
  input  hit_miss,
  output out_3
);

  wire clock_1_out, comparator_1_gt, not_1_out, xor_1_out, xor_2_out, xor_3_out, xor_4_out;
  wire [3:0] adder_1_out, adder_2_out, adder_3_out, adder_4_out, adder_5_out, adder_6_out, adder_7_out,
       adder_8_out, adder_9_out, demultiplexer_1_out0, demultiplexer_1_out0_2, demultiplexer_1_out0_3,
       demultiplexer_1_out0_4, demultiplexer_1_out0_5, demultiplexer_1_out1_2, GHR_out_3, multiplexer_2_out,
       multiplexer_3_out, multiplexer_4_out, multiplexer_5_out, negator_1_out, negator_2_out, negator_3_out,
       negator_4_out, PC_out_3, Score__u_q, subtractor_1_out, subtractor_2_out, subtractor_3_out,
       subtractor_4_out, subtractor_5_out;
  wire [19:0] demultiplexer_1_out1, ram_1_data;

  Clock clock_1 (.out(clock_1_out));
  PC PC (.in_1(clock_1_out), .out_3(PC_out_3));  // open: in_2
  GHR GHR (.clk(clock_1_out), .entrada(hit_miss), .out_3(GHR_out_3));
  not not_1 (not_1_out, out_3);
  RAM #(.addrWidth(4), .dataWidth(20), .bus("asynch")) ram_1 (
    .addr(PC_out_3), .data(ram_1_data), .ld(not_1_out), .clr(in_1));  // open: sel
  xor xor_1 (xor_1_out, GHR_out_3[0], hit_miss);
  Demultiplexer #(.width(20), .enable("false")) demultiplexer_1 (
    .out0({demultiplexer_1_out0_5, demultiplexer_1_out0_4, demultiplexer_1_out0_3, demultiplexer_1_out0_2, demultiplexer_1_out0}),
    .out1({demultiplexer_1_out1[19:12], demultiplexer_1_out1_2, demultiplexer_1_out1[7:0]}), .in(ram_1_data),
    .sel(out_3));
  Subtractor #(.width(4)) subtractor_1 (
    .a(demultiplexer_1_out0_5), .b(4'b0001), .out(subtractor_1_out));  // open: bin, bout
  Adder #(.width(4)) adder_1 (.a(demultiplexer_1_out0_5), .b(4'b0001), .out(adder_1_out));  // open: cin, cout
  Multiplexer #(.width(4), .enable("false")) multiplexer_1 (
    .in0(subtractor_1_out), .in1(adder_1_out), .out(demultiplexer_1_out1[19:16]), .sel(xor_1_out));
  xor xor_2 (xor_2_out, GHR_out_3[1], hit_miss);
  xor xor_3 (xor_3_out, GHR_out_3[2], hit_miss);
  Multiplexer #(.width(4), .enable("false")) multiplexer_2 (
    .in0(demultiplexer_1_out0_2), .in1(negator_1_out), .out(multiplexer_2_out), .sel(GHR_out_3[0]));
  Negator #(.width(4)) negator_1 (.in(demultiplexer_1_out0_2), .out(negator_1_out));
  Negator #(.width(4)) negator_2 (.in(demultiplexer_1_out0_3), .out(negator_2_out));
  Negator #(.width(4)) negator_3 (.in(demultiplexer_1_out0_4), .out(negator_3_out));
  Negator #(.width(4)) negator_4 (.in(demultiplexer_1_out0_5), .out(negator_4_out));
  Subtractor #(.width(4)) subtractor_2 (
    .a(demultiplexer_1_out0_4), .b(4'b0001), .out(subtractor_2_out));  // open: bin, bout
  Adder #(.width(4)) adder_2 (.a(demultiplexer_1_out0_4), .b(4'b0001), .out(adder_2_out));  // open: cin, cout
  Subtractor #(.width(4)) subtractor_3 (
    .a(demultiplexer_1_out0_3), .b(4'b0001), .out(subtractor_3_out));  // open: bin, bout
  Adder #(.width(4)) adder_3 (.a(demultiplexer_1_out0_3), .b(4'b0001), .out(adder_3_out));  // open: cin, cout
  xor xor_4 (xor_4_out, GHR_out_3[3], hit_miss);
  Multiplexer #(.width(4), .enable("false")) multiplexer_3 (
    .in0(demultiplexer_1_out0_3), .in1(negator_2_out), .out(multiplexer_3_out), .sel(GHR_out_3[1]));
  Multiplexer #(.width(4), .enable("false")) multiplexer_4 (
    .in0(demultiplexer_1_out0_4), .in1(negator_3_out), .out(multiplexer_4_out), .sel(GHR_out_3[2]));
  Multiplexer #(.width(4), .enable("false")) multiplexer_5 (
    .in0(demultiplexer_1_out0_5), .in1(negator_4_out), .out(multiplexer_5_out), .sel(GHR_out_3[3]));
  Multiplexer #(.width(4), .enable("false")) multiplexer_6 (
    .in0(subtractor_2_out), .in1(adder_2_out), .out(demultiplexer_1_out1[15:12]), .sel(xor_2_out));
  Multiplexer #(.width(4), .enable("false")) multiplexer_7 (
    .in0(subtractor_3_out), .in1(adder_3_out), .out(demultiplexer_1_out1_2), .sel(xor_3_out));
  Subtractor #(.width(4)) subtractor_4 (
    .a(demultiplexer_1_out0_2), .b(4'b0001), .out(subtractor_4_out));  // open: bin, bout
  Adder #(.width(4)) adder_4 (.a(demultiplexer_1_out0_2), .b(4'b0001), .out(adder_4_out));  // open: cin, cout
  Subtractor #(.width(4)) subtractor_5 (
    .a(demultiplexer_1_out0), .b(4'b0001), .out(subtractor_5_out));  // open: bin, bout
  Adder #(.width(4)) adder_5 (.a(demultiplexer_1_out0), .b(4'b0001), .out(adder_5_out));  // open: cin, cout
  Multiplexer #(.width(4), .enable("false")) multiplexer_8 (
    .in0(subtractor_4_out), .in1(adder_4_out), .out(demultiplexer_1_out1[7:4]), .sel(xor_4_out));
  Adder #(.width(4)) adder_6 (.a(multiplexer_3_out), .b(multiplexer_4_out), .out(adder_6_out));  // open: cin, cout
  Multiplexer #(.width(4), .enable("false")) multiplexer_9 (
    .in0(subtractor_5_out), .in1(adder_5_out), .out(demultiplexer_1_out1[3:0]), .sel(hit_miss));
  Adder #(.width(4)) adder_7 (.a(demultiplexer_1_out0), .b(multiplexer_2_out), .out(adder_7_out));  // open: cin, cout
  Adder #(.width(4)) adder_8 (.a(adder_6_out), .b(multiplexer_5_out), .out(adder_8_out));  // open: cin, cout
  Adder #(.width(4)) adder_9 (.a(adder_7_out), .b(adder_8_out), .out(adder_9_out));  // open: cin, cout
  Register #(.width(4)) Score__u (.D(adder_9_out), .Q(Score__u_q));  // open: en, clk, clr
  Comparator #(.width(4)) comparator_1 (.a(Score__u_q), .b(4'b0000), .gt(comparator_1_gt));  // open: eq, lt
  xor xor_5 (out_3, comparator_1_gt, hit_miss);

  // Notes on the sheet:
  //   32 bits
  //   /
  //   11:2
  //   10  bits
  //   /
  //   W_i(novo) = W_i(atual) + (d*x_i)
  //   Tabela de Pesos
  //   -1
  //   8 bits
  //   /
  //   8 bits
  //   /
  //   8 bits
  //   /
  //   W(1)
  //   -1
  //   -1
  //   -1
  //   W(2)
  //   W(3)
  //   W(4)
  //   BIAS
  //   W(1)_novo
  //   BIAS
  //   somador Σ
endmodule

module GHR (
  input  clk,
  input  entrada,
  output [3:0] out_3
);

  D_Flip_Flop GHR_3 (.clk(clk), .D(entrada), .Q(out_3[3]));  // open: Qn, preset, en, reset
  D_Flip_Flop GHR_1 (.clk(clk), .D(out_3[2]), .Q(out_3[1]));  // open: Qn, preset, en, reset
  D_Flip_Flop GHR_2 (.clk(clk), .D(out_3[3]), .Q(out_3[2]));  // open: Qn, preset, en, reset
  D_Flip_Flop GHR_0 (.clk(clk), .D(out_3[1]), .Q(out_3[0]));  // open: Qn, preset, en, reset
endmodule

module PC (
  input  in_1,
  input  in_2,
  output [3:0] out_3
);

  Counter #(.width(4), .max('hf)) counter_1 (.Q(out_3), .clk(in_1), .clr(in_2));  // open: load, D, count, carry
endmodule
